// Logisim project cpu.circ as structural Verilog: 3 circuits, main circuit cpu
module cpu (
  input  clk,
  input  [31:0] INSTRUCTION,
  input  [31:0] READ_DATA,
  output [31:0] WRITE_ADDRESS,
  output [31:0] PROGRAM_COUNTER,
  output [31:0] ra,
  output [31:0] sp,
  output [31:0] t0,
  output [31:0] t1,
  output [31:0] t2,
  output [31:0] s0,
  output [31:0] s1,
  output [31:0] a0,
  output [31:0] tohost,
  output [3:0] WRITE_ENABLE,
  output [31:0] WRITE_DATA
);

  wire ASel, BrEq, BrLt, BrUn, BSel, CSRSel, CSRWen, MemRW, PCSel, RegWEn;
  wire [1:0] WBSel;
  wire [2:0] ImmSel;
  wire [3:0] ALUSel, write_enable_t;
  wire [11:0] CSR_address;
  wire [31:0] A, B, CSR_din, imm, pc, pc_4, read_data1, register_write;

  Adder #(.width(32)) adder_1 (.a(PROGRAM_COUNTER), .b(32'h4), .out(pc_4));  // open: cin, cout
  Register #(.width(32)) u_PC (.D(pc), .clk(clk), .Q(PROGRAM_COUNTER));  // open: en, clr
  Multiplexer #(.enable("false"), .width(32)) multiplexer_1 (.in0(pc_4), .in1(WRITE_ADDRESS), .out(pc), .sel(PCSel));
  // Probe on imm
  // Probe on write_enable_t
  imm_gen imm_gen_1 (.inst(INSTRUCTION), .ImmSel(ImmSel), .imm(imm));
  control_logic control_logic_1 (
    .CSRWen(CSRWen), .write_enable(write_enable_t), .out_5(PCSel), .RegWEn(RegWEn), .ImmSel(ImmSel),
    .BrUn(BrUn), .ASel(ASel), .BSel(BSel), .ALUSel(ALUSel), .MemRW(MemRW), .WBSel(WBSel), .CSRSel(CSRSel),
    .inst(INSTRUCTION), .BrEq(BrEq), .BrLt(BrLt));
  regfile regfile_1 (
    .rs1(INSTRUCTION[19:15]), .rs2(INSTRUCTION[24:20]), .rd(INSTRUCTION[11:7]), .Write_Data(register_write),
    .RegWEn(RegWEn), .clk(clk), .ra(ra), .sp(sp), .t0(t0), .t1(t1), .t2(t2), .s0(s0), .s1(s1), .a0(a0),
    .Read_Data_1(read_data1), .Read_Data_2(WRITE_DATA));
  branch_comp branch_comp_1 (.rs1(read_data1), .rs2(WRITE_DATA), .BrUn(BrUn), .BrEq(BrEq), .BrLt(BrLt));
  // csr csr_1: pin names not known; wires that end beside it: CSR_address, CSR_din, CSRWen, clk, tohost
  // Probe on WBSel
  alu alu_1 (.Result(WRITE_ADDRESS), .A(A), .B(B), .ALUSel(ALUSel));
  // Probe on WRITE_ADDRESS
  CSR_Decode csr_decode_1 (
    .CSRSel(CSRSel), .Inst(INSTRUCTION), .rs1(read_data1), .CSR_address(CSR_address), .CSR_din(CSR_din));
  Multiplexer #(.enable("false"), .width(4)) multiplexer_2 (
    .in0(4'b0000), .in1(write_enable_t), .out(WRITE_ENABLE), .sel(MemRW));
  ABSel absel_1 (
    .ASel(ASel), .BSel(BSel), .rs1(read_data1), .rs2(WRITE_DATA), .imm(imm), .pc(PROGRAM_COUNTER), .A(A),
    .B(B));
  // Probe on register_write
  Multiplexer #(.enable("false"), .select(2), .width(32)) multiplexer_3 (
    .in0(READ_DATA), .in1(WRITE_ADDRESS), .in2(pc_4), .out(register_write), .sel(WBSel));  // open: in3

  // Other names for the same wires on the sheet: ALU_result[31:0] = WRITE_ADDRESS; rd[4:0] = INSTRUCTION[11:7];
  //   rs1[4:0] = INSTRUCTION[19:15]; rs2[4:0] = INSTRUCTION[24:20]; read_data2[31:0] = WRITE_DATA

  // Notes on the sheet:
  //   Output to IMEM
  //   IMEM (do **NOT** move this)
  //   Inputs from IMEM
  //   It is OK to move the PC, RegFile, ALU, MEM, Branch Comp, Imm Gen, and Control Logic to wherever is most convenient for you when constructing your CPU, and to delete this text
  //   Inputs/Outputs for testing. Do **NOT** move these.
  //   Outputs To DMEM
  //   DMEM (do **NOT** move this)
  //   Inputs From DMEM
endmodule

module CSR_Decode (
  input  CSRSel,
  input  [31:0] Inst,
  input  [31:0] rs1,
  output [11:0] CSR_address,
  output [31:0] CSR_din
);

  wire [31:0] imm;

  assign imm = {{27{1'b0}}, Inst[19:15]};  // Bit_Extender bit_extender_1
  Multiplexer #(.enable("false"), .width(32)) multiplexer_1 (.in0(rs1), .in1(imm), .out(CSR_din), .sel(CSRSel));

  assign CSR_address = Inst[31:20];
endmodule

module ABSel (
  input  ASel,
  input  BSel,
  input  [31:0] rs1,
  input  [31:0] rs2,
  input  [31:0] imm,
  input  [31:0] pc,
  output [31:0] A,
  output [31:0] B
);

  Multiplexer #(.enable("false"), .width(32)) multiplexer_1 (.in0(rs1), .in1(pc), .out(A), .sel(ASel));
  Multiplexer #(.enable("false"), .width(32)) multiplexer_2 (.in0(rs2), .in1(imm), .out(B), .sel(BSel));
endmodule
